# Fritzing sketch TinyWireMCP23008 (saved by Fritzing 0.8.3b)
breadboards: 1

parts:
  IC1 = Microchip MCP23008 8-bit I/O expander [part_number=MCP23008 package="DIP (Dual Inline) [THT]"]
  U1 = attiny85 [package=dip]
  R1 = Resistor [tolerance=±5% resistance=330 package=THT]
  LED1 = LED - 5mm [color="Red (633nm)" package="5 mm [THT]"]
  JACK1 = 2.1mm Barrel Jack with Terminal Block
  R2 = Resistor [tolerance=±5% resistance=4.7k package=THT]
  R3 = Resistor [tolerance=±5% resistance=4.7k package=THT]

nets:
  N1: IC1.SCL, U1.Pin_7, R2.Pin_1
  N2: IC1.SDA, U1.Pin_5, R3.Pin_1
  N3: IC1.A2, IC1.A1, IC1.A0, IC1.VSS, U1.Pin_4, LED1.cathode, JACK1.NEG
  N4: IC1.Reset, IC1.VDD, U1.Pin_8, JACK1.POS, R2.Pin_0, R3.Pin_0
  N5: IC1.GP0, R1.Pin_0
  N6: R1.Pin_1, LED1.anode

notes:
  +5V source

custom parts:
  Microchip MCP23008 8-bit I/O expander: Provides 8-bit, general purpose, parallel I/O expansion for I2C bus. Datasheet: http://ww1.microchip.com/downloads/en/devicedoc/21919e.pdf
